// Logisim project cpuPic.circ as structural Verilog
module adder_32bits (
  input  in_1,
  input  [31:0] in_2,
  input  [31:0] in_3,
  output [31:0] out_4,
  output out_5
);

  wire adder_1_cout, adder_2_cout, adder_3_cout;

  Adder adder_1 (.a(in_2[7:0]), .b(in_3[7:0]), .out(out_4[7:0]), .cin(in_1), .cout(adder_1_cout));
  Adder adder_2 (.a(in_2[15:8]), .b(in_3[15:8]), .out(out_4[15:8]), .cin(adder_1_cout), .cout(adder_2_cout));
  Adder adder_3 (.a(in_2[23:16]), .b(in_3[23:16]), .out(out_4[23:16]), .cin(adder_2_cout), .cout(adder_3_cout));
  Adder adder_4 (.a(in_2[31:24]), .b(in_3[31:24]), .out(out_4[31:24]), .cin(adder_3_cout), .cout(out_5));
endmodule

module invert (
  input  [31:0] in_1,
  input  in_2,
  output [31:0] out_3
);

  assign out_3[31:24] = {8{in_2}} ^ in_1[31:24];  // XOR_Gate xor_1, 8 bits wide
  assign out_3[23:16] = {8{in_2}} ^ in_1[23:16];  // XOR_Gate xor_2, 8 bits wide
  assign out_3[15:8] = {8{in_2}} ^ in_1[15:8];  // XOR_Gate xor_3, 8 bits wide
  assign out_3[7:0] = {8{in_2}} ^ in_1[7:0];  // XOR_Gate xor_4, 8 bits wide
endmodule

module minus (
  input  [31:0] x2,
  input  [31:0] x1,
  input  en,
  output [31:0] bout,
  output en_b
);

  wire adder_32bits_1_out_5;
  wire [31:0] invert_1_out_3;

  invert invert_1 (.in_1(x1), .in_2(en), .out_3(invert_1_out_3));
  adder_32bits adder_32bits_1 (.in_1(en), .in_2(x2), .in_3(invert_1_out_3), .out_5(adder_32bits_1_out_5), .out_4(bout));
  not not_1 (en_b, adder_32bits_1_out_5);
endmodule

module segment_display (
  input  [7:0] in_1
);

  wire [7:0] rom_1_data;

  ROM rom_1 (.addr(in_1), .data(rom_1_data));
  _7_Segment_Display u_7_segment_display_1 (
    .g(rom_1_data[0]), .f(rom_1_data[1]), .a(rom_1_data[2]), .b(rom_1_data[3]), .e(rom_1_data[4]),
    .d(rom_1_data[5]), .c(rom_1_data[6]), .dp(rom_1_data[7]));

  // Notes on the sheet:
  //   contents of rom_1 (hex, n*v repeats v):
  //   7e 48 3d 6d 4b 67 77 4c 7f 6f
endmodule

module BIN_to_BCD (
  input  [3:0] BIN_4bit,
  output [3:0] BCD_4bit
);

  wire adder_1_cout, adder_2_cout, adder_3_cout, and_1_out, or_1_out, or_2_out, or_3_out;

  or or_1 (or_1_out, BIN_4bit[0], BIN_4bit[1]);
  and and_1 (and_1_out, or_1_out, or_2_out);
  or or_2 (or_2_out, BIN_4bit[2], BIN_4bit[3]);
  or or_3 (or_3_out, and_1_out, BIN_4bit[3]);
  Adder #(.width(1)) adder_1 (.a(BIN_4bit[0]), .b(or_3_out), .out(BCD_4bit[0]), .cin(1'b0), .cout(adder_1_cout));
  Adder #(.width(1)) adder_2 (
    .a(BIN_4bit[1]), .b(or_3_out), .out(BCD_4bit[1]), .cin(adder_1_cout), .cout(adder_2_cout));
  Adder #(.width(1)) adder_3 (.a(BIN_4bit[2]), .b(1'b0), .out(BCD_4bit[2]), .cin(adder_2_cout), .cout(adder_3_cout));
  Adder #(.width(1)) adder_4 (.a(BIN_4bit[3]), .b(1'b0), .out(BCD_4bit[3]), .cin(adder_3_cout));  // open: cout

  // Notes on the sheet:
  //   no,we may not need this
  //   BIN to BCD -> when BIN = 5 +> +3
endmodule

module BIN_BCD_0to9_forSegment (
  input  [13:0] in_1,
  output [15:0] out_2
);

  wire [0:0] bin_to_bcd_4_bcd_4bit_2;
  wire [2:0] bin_to_bcd_1_bcd_4bit, bin_to_bcd_2_bcd_4bit, bin_to_bcd_3_bcd_4bit, bin_to_bcd_3_bcd_4bit_2;
  wire [3:0] bin_to_bcd_5_bcd_4bit, bin_to_bcd_6_bcd_4bit, bin_to_bcd_7_bcd_4bit, bin_to_bcd_8_bcd_4bit,
       bin_to_bcd_9_bcd_4bit, bin_to_bcd_10_bcd_4bit, bin_to_bcd_11_bcd_4bit, bin_to_bcd_12_bcd_4bit,
       bin_to_bcd_13_bcd_4bit, bin_to_bcd_14_bcd_4bit;
  wire [3:1] bin_to_bcd_4_bcd_4bit;
  wire [3:2] bin_to_bcd_18_bcd_4bit;

  BIN_to_BCD bin_to_bcd_1 (
    .BIN_4bit({1'b0, in_1[13:11]}), .BCD_4bit({bin_to_bcd_3_bcd_4bit_2[2], bin_to_bcd_1_bcd_4bit}));
  BIN_to_BCD bin_to_bcd_2 (
    .BIN_4bit({bin_to_bcd_1_bcd_4bit, in_1[10]}),
    .BCD_4bit({bin_to_bcd_3_bcd_4bit_2[1], bin_to_bcd_2_bcd_4bit}));
  BIN_to_BCD bin_to_bcd_3 (
    .BIN_4bit({bin_to_bcd_2_bcd_4bit, in_1[9]}),
    .BCD_4bit({bin_to_bcd_3_bcd_4bit_2[0], bin_to_bcd_3_bcd_4bit}));
  BIN_to_BCD bin_to_bcd_4 (
    .BIN_4bit({bin_to_bcd_3_bcd_4bit, in_1[8]}),
    .BCD_4bit({bin_to_bcd_4_bcd_4bit_2[0], bin_to_bcd_4_bcd_4bit}));
  BIN_to_BCD bin_to_bcd_5 (.BIN_4bit({bin_to_bcd_4_bcd_4bit, in_1[7]}), .BCD_4bit(bin_to_bcd_5_bcd_4bit));
  BIN_to_BCD bin_to_bcd_6 (.BIN_4bit({1'b0, bin_to_bcd_3_bcd_4bit_2}), .BCD_4bit(bin_to_bcd_6_bcd_4bit));
  BIN_to_BCD bin_to_bcd_7 (.BIN_4bit({bin_to_bcd_5_bcd_4bit[2:0], in_1[6]}), .BCD_4bit(bin_to_bcd_7_bcd_4bit));
  BIN_to_BCD bin_to_bcd_8 (
    .BIN_4bit({bin_to_bcd_6_bcd_4bit[2:0], bin_to_bcd_4_bcd_4bit_2[0]}), .BCD_4bit(bin_to_bcd_8_bcd_4bit));
  BIN_to_BCD bin_to_bcd_9 (.BIN_4bit({bin_to_bcd_7_bcd_4bit[2:0], in_1[5]}), .BCD_4bit(bin_to_bcd_9_bcd_4bit));
  BIN_to_BCD bin_to_bcd_10 (
    .BIN_4bit({bin_to_bcd_8_bcd_4bit[1:0], bin_to_bcd_5_bcd_4bit[3], bin_to_bcd_7_bcd_4bit[3]}),
    .BCD_4bit(bin_to_bcd_10_bcd_4bit));
  BIN_to_BCD bin_to_bcd_11 (
    .BIN_4bit({1'b0, bin_to_bcd_6_bcd_4bit[3], bin_to_bcd_8_bcd_4bit[3:2]}), .BCD_4bit(bin_to_bcd_11_bcd_4bit));
  BIN_to_BCD bin_to_bcd_12 (.BIN_4bit({bin_to_bcd_9_bcd_4bit[1:0], in_1[4:3]}), .BCD_4bit(bin_to_bcd_12_bcd_4bit));
  BIN_to_BCD bin_to_bcd_13 (
    .BIN_4bit({bin_to_bcd_10_bcd_4bit[1:0], bin_to_bcd_9_bcd_4bit[3:2]}), .BCD_4bit(bin_to_bcd_13_bcd_4bit));
  BIN_to_BCD bin_to_bcd_14 (
    .BIN_4bit({bin_to_bcd_11_bcd_4bit[1:0], bin_to_bcd_10_bcd_4bit[3:2]}), .BCD_4bit(bin_to_bcd_14_bcd_4bit));
  BIN_to_BCD bin_to_bcd_15 (.BIN_4bit({bin_to_bcd_12_bcd_4bit[2:0], in_1[2]}), .BCD_4bit(out_2[5:2]));
  BIN_to_BCD bin_to_bcd_16 (.BIN_4bit({bin_to_bcd_13_bcd_4bit[2:0], bin_to_bcd_12_bcd_4bit[3]}), .BCD_4bit(out_2[9:6]));
  BIN_to_BCD bin_to_bcd_17 (
    .BIN_4bit({bin_to_bcd_14_bcd_4bit[2:0], bin_to_bcd_13_bcd_4bit[3]}), .BCD_4bit(out_2[13:10]));
  // NoConnect on bin_to_bcd_18_bcd_4bit[2]
  // NoConnect on bin_to_bcd_18_bcd_4bit[3]
  BIN_to_BCD bin_to_bcd_18 (
    .BIN_4bit({1'b0, bin_to_bcd_11_bcd_4bit[3:2], bin_to_bcd_14_bcd_4bit[3]}),
    .BCD_4bit({bin_to_bcd_18_bcd_4bit, out_2[15:14]}));

  assign out_2[1:0] = in_1[1:0];
endmodule

module divisor (
  input  CP_in,
  output CP,
  output CP_div4,
  output CP_div2
);

  wire d_ff_1_qn, d_ff_2_qn;

  D_Flip_Flop d_ff_1 (.D(d_ff_1_qn), .clk(CP_in), .Q(CP_div2), .Qn(d_ff_1_qn));  // open: preset, reset
  D_Flip_Flop d_ff_2 (.D(d_ff_2_qn), .clk(CP_div2), .Q(CP_div4), .Qn(d_ff_2_qn));  // open: preset, reset

  assign CP = CP_in;
endmodule

module memory (
  input  [7:0] din,
  input  CP,
  input  RST,
  input  W,
  input  [1:0] WAddr,
  input  R,
  input  [1:0] RAddr,
  output [7:0] dout
);

  wire demultiplexer_1_out0, demultiplexer_1_out1, demultiplexer_1_out2, demultiplexer_1_out3,
       demultiplexer_2_out0, demultiplexer_2_out1, demultiplexer_2_out2, demultiplexer_2_out3;
  wire [7:0] controlled_buffer_1_out, controlled_buffer_2_out, controlled_buffer_3_out, register_1_q,
       register_2_q, register_3_q, register_4_q;

  Demultiplexer #(.select(2)) demultiplexer_1 (
    .out0(demultiplexer_1_out0), .out1(demultiplexer_1_out1), .out2(demultiplexer_1_out2),
    .out3(demultiplexer_1_out3), .in(W), .sel(WAddr));
  Demultiplexer #(.select(2)) demultiplexer_2 (
    .out0(demultiplexer_2_out0), .out1(demultiplexer_2_out1), .out2(demultiplexer_2_out2),
    .out3(demultiplexer_2_out3), .in(R), .sel(RAddr));
  Register register_1 (.D(din), .en(demultiplexer_2_out0), .clk(CP), .Q(register_1_q), .clr(RST));
  Register register_2 (.D(controlled_buffer_1_out), .en(demultiplexer_2_out1), .clk(CP), .Q(register_2_q), .clr(RST));
  assign controlled_buffer_1_out = demultiplexer_1_out0 ? register_1_q : 8'bz;  // Controlled_Buffer controlled_buffer_1
  Register register_3 (.D(controlled_buffer_2_out), .en(demultiplexer_2_out2), .clk(CP), .Q(register_3_q), .clr(RST));
  assign controlled_buffer_2_out = demultiplexer_1_out1 ? register_2_q : 8'bz;  // Controlled_Buffer controlled_buffer_2
  Register register_4 (.D(controlled_buffer_3_out), .en(demultiplexer_2_out3), .clk(CP), .Q(register_4_q), .clr(RST));
  assign controlled_buffer_3_out = demultiplexer_1_out2 ? register_3_q : 8'bz;  // Controlled_Buffer controlled_buffer_3
  assign dout = demultiplexer_1_out3 ? register_4_q : 8'bz;  // Controlled_Buffer controlled_buffer_4
endmodule
